# Fritzing sketch schema (saved by Fritzing 0.9.3b)

parts:
  WeMos_D1_Mini2 = WeMos D1 Mini
  C1 = Ceramic Capacitor [capacitance=100nF package="100 mil [THT, multilayer]"]
  C2 = Electrolytic Capacitor [capacitance=47µF package="100 mil [THT, electrolytic]"]
  D2 = Diode [package=diode-1n4148]
  R1 = Resistor [tolerance=±5% resistance=1.5k package=THT]
  J2 = Basic Servo
  J3 = Power Jack [package=power_jack_pth_lock]

nets:
  N1: WeMos_D1_Mini2.5V, C1.1, D2.C
  N2: WeMos_D1_Mini2.D2, R1.Pin_1
  GND: WeMos_D1_Mini2.G, C1.0, C2.-, J2.gnd, J3.GND
  N3: C2.+, D2.A, J2.vcc, J3.PWR
  N4: R1.Pin_0, J2.pulse
